# Fritzing sketch rlc project (saved by Fritzing 0.8.5b)
breadboards: 1

parts:
  Tlc2 = Packages: [package=dil28-3]
  U4 = atmega328 [package=dip]
  Tlc4 = Packages: [package=dil28-3]
  U7 = ATTINY45 [package=dip]  # not connected
  CONN1 = USB connector [package=THT]  # not connected
  Tlc1 = Packages: [package=dil28-3]
  J1 = Power Jack [package=power_jack_smd]  # not connected
  R1 = Resistor [tolerance=±5% resistance=2k package=THT]  # not connected
  R2 = Resistor [tolerance=±5% resistance=2k package=THT]  # not connected
  R5 = Resistor [tolerance=±5% resistance=2k package=THT]  # not connected
  R6 = Resistor [tolerance=±5% resistance=2k package=THT]  # not connected
  Tlc3 = Packages: [package=dil28-3]
  R7 = Resistor [tolerance=±5% resistance=2k package=THT]
  R8 = Resistor [tolerance=±5% resistance=2k package=THT]
  R9 = Resistor [tolerance=±5% resistance=2k package=THT]
  R10 = Resistor [tolerance=±5% resistance=2k package=THT]

nets:
  N1: Tlc2.XERR, Tlc2.SOUT, Tlc1.SIN
  N2: Tlc2.GSCLK, U4.D3_(PWM)
  N3: Tlc2.IREF, R7.Pin_0
  VCC: Tlc2.VCC, U4.VCC, Tlc4.VCC, Tlc1.VCC, Tlc3.VCC
  GND: Tlc2.GND, Tlc2.BLANK, U4.D10_(PWM), U4.GND, Tlc4.GND, Tlc4.BLANK, Tlc1.GND, Tlc1.BLANK, Tlc3.GND, Tlc3.BLANK, R7.Pin_1, R8.Pin_1, R9.Pin_1, R10.Pin_1
  N4: Tlc2.XLAT, U4.D9_(PWM), Tlc4.XLAT, Tlc1.XLAT, Tlc3.XLAT, Tlc3.SCLK
  N5: Tlc2.SCLK, U4.D13
  N6: Tlc2.SIN, U4.D11_(PWM)
  N7: Tlc4.IREF, R10.Pin_0
  N8: Tlc4.SIN, Tlc3.SOUT, Tlc3.GSCLK
  N9: Tlc1.SOUT, Tlc3.SIN, Tlc3.VPRG
  N10: Tlc1.IREF, R8.Pin_0
  N11: Tlc3.IREF, R9.Pin_0
